// Digital circuit main.dig as structural Verilog
module main (
  input  clk,
  input  [7:0] in_2,
  input  [7:0] in_3,
  input  in_4,
  input  in_6,
  input  in_7,
  output [7:0] out_5
);

  wire [7:0] u_adder_8bit_sum;

  adder_8bit #(.applicationType("IVERILOG"), .CodeFile("/home/kaldwin/Development/Projects/the_electronics_project_misc/src/adder_8bit.v")) u_adder_8bit (
    .a(in_2), .b(in_3), .cin(in_6), .sum(u_adder_8bit_sum));  // open: cout
  register_8bit #(.applicationType("IVERILOG"), .CodeFile("/home/kaldwin/Development/Projects/the_electronics_project_misc/src/register_8bit.v")) u_register_8bit (
    .clk(clk), .reset(in_7), .write(in_4), .data_in(u_adder_8bit_sum), .data_out(out_5));

  // Notes on the sheet:
  //   clk: Hz: 50
endmodule
